# Fritzing sketch SignalGenerator (saved by Fritzing 0.9.9b)
breadboards: 1

parts:
  Grove1 = Grove OLED 128x96
  R1 = Resistor [tolerance=±5% resistance=10k package="2512 [SMD]"]
  R2 = Resistor [tolerance=±5% resistance=10k package="2512 [SMD]"]
  R3 = Resistor [tolerance=±5% resistance=10k package="2512 [SMD]"]
  R4 = Resistor [tolerance=±5% resistance=10k package="2512 [SMD]"]
  Součástka1 = Arduino Uno (Rev3)
  S1 = Pushbutton [package="[SMD]"]
  S2 = Pushbutton [package="[SMD]"]
  S3 = Pushbutton [package="[SMD]"]
  S4 = Pushbutton [package="[SMD]"]
  AD1 = DDS AD9850

nets:
  GND: Grove1.GND, R1.Pin_1, R2.Pin_1, R3.Pin_1, R4.Pin_1, Součástka1.GND, AD1.GND
  VCC: Grove1.VCC, Součástka1.3V3
  N1: Grove1.SDA, Součástka1.A4/SDA
  N2: Grove1.SCL, Součástka1.A5/SCL
  N3: R1.Pin_0, Součástka1.D2, S4.Pin_1, S4.Pin_2
  N4: R2.Pin_0, Součástka1.D3_PWM, S3.Pin_1, S3.Pin_2
  N5: R3.Pin_0, Součástka1.D5_PWM, S1.Pin_1, S1.Pin_2
  N6: R4.Pin_0, Součástka1.D4, S2.Pin_1, S2.Pin_2
  N7: Součástka1.D11_PWM/MOSI, AD1.DATA
  N8: Součástka1.D13/SCK, AD1.CLK
  N9: Součástka1.D6_PWM, AD1.FQ
  N10: Součástka1.D7, AD1.RST
  5V: Součástka1.5V, S1.Pin_3, S1.Pin_4, S2.Pin_3, S2.Pin_4, S3.Pin_3, S3.Pin_4, S4.Pin_3, S4.Pin_4, AD1.VCC

custom parts:
  DDS AD9850: AD9850 DDS Signal Generator Module, frequency range 0 to 40MHz, sine or square wave output, on board 70MHz low pass filter, and 125MHz clock module. https://code.google.com/p/ad9850-arduino/
